# Fritzing sketch rpi (saved by Fritzing 0.9.3b)
breadboards: 1

parts:
  Raspberry_Pi_1 = Raspberry Pi 3 [part_number=RPI-3-V1.2]
  J1 = Basic Servo
  J2 = Basic Servo
  J4 = Basic Servo
  J3 = Basic Servo

nets:
  N1: Raspberry_Pi_1.GIPO4, J2.pulse
  N2: Raspberry_Pi_1.GIPO17, J4.pulse
  N3: Raspberry_Pi_1.GIPO27, J3.pulse
  N4: Raspberry_Pi_1.GIPO18, J1.pulse
  GND: Raspberry_Pi_1.GND, J1.gnd, J2.gnd, J4.gnd, J3.gnd
  VCC: Raspberry_Pi_1.5V, J1.vcc, J2.vcc, J4.vcc, J3.vcc

notes:
  Left
  Right
  Middle
  Claw
